# Fritzing sketch DigitalClock (saved by Fritzing 0.8.7b)
breadboards: 1

parts:
  WeMos_D1_Mini1 = WeMos D1 Mini
  R1 = Photocell (LDR) [package=THT]
  VCC = Header 1 [package=smtso-256-et]
  R2 = Resistor [tolerance=±5% resistance=10k package=THT]
  GND = Header 1 [package=smtso-256-et]
  DATA_LEDS = Header 1 [package=smtso-256-et]
  J1 = Piezo Speaker
  Q1 = NPN-Transistor [package="TO92 [THT]"]
  ZS-042_RTC1 = ZS-042 RTC Module
  R3 = Resistor [tolerance=±5% resistance=100 package=THT]

nets:
  N1: WeMos_D1_Mini1.5V, VCC.1
  N2: WeMos_D1_Mini1.A0, R1.pin_0, R2.Pin_0
  N3: WeMos_D1_Mini1.D4, DATA_LEDS.1
  N4: WeMos_D1_Mini1.D5, R3.Pin_0
  N5: WeMos_D1_Mini1.G, GND.1, Q1.E, ZS-042_RTC1.GND
  N6: R1.pin_1, J1.pin2, ZS-042_RTC1.VCC
  N7: J1.pin1, Q1.C
  N8: Q1.B, R3.Pin_1

custom parts:
  WeMos D1 Mini: The D1 mini is a mini wifi board based on ESP-8266EX.
